# Fritzing sketch Diagrama (saved by Fritzing 0.9.3b)
breadboards: 1

parts:
  Componente1 = Arduino Uno (Rev3)
  LED1 = LED - 5mm [color="Red (633nm)" package="5 mm [THT]"]
  R1 = Resistor [tolerance=±5% resistance=220 package=THT]
  R2 = Resistor [tolerance=±5% resistance=10k package=THT]
  S1 = Pushbutton [package=THT]

nets:
  N1: Componente1.D2, R2.Pin_1, S1.leg0
  N2: Componente1.D3_PWM, LED1.anode
  N3: Componente1.5V, S1.leg1
  N4: Componente1.GND, R1.Pin_0, R2.Pin_0
  N5: LED1.cathode, R1.Pin_1
